# Fritzing sketch MQTT_Tanklevelsensor.ino (saved by Fritzing 0.9.3b)
circuit board: 8.46667cm x 5.64444cm
breadboards: 1

parts:
  WeMos_D1_Mini1 = WeMos D1 Mini
  DHT22 = DHT22 Humidity and Temperature Sensor
  U3 = HC-SR04 [chip_label=IC package="SIP (Single Inline) [THT]"]
  R2 = Resistor [tolerance=±5% resistance=220 package="1206 [SMD]"]
  C1 = Ceramic Capacitor [capacitance="100 nF" package="0603 [SMD, multilayer]"]
  R4 = Resistor [tolerance=±5% resistance=10k package="1206 [SMD]"]
  TP4056 = TP4056 [chip_label=TP4056 package="DIP (Dual Inline) [THT]"]
  U4 = LIPO-1000mAh [package=lipo-1000]
  D1 = SOLAR-IXYS [package=solarbit-12x1]

nets:
  3V3: WeMos_D1_Mini1.3V3, DHT22.VDD, R4.Pin_1
  5V: WeMos_D1_Mini1.5V, WeMos_D1_Mini1.A0, U3.Vcc, TP4056.pin3
  N1: WeMos_D1_Mini1.D0, WeMos_D1_Mini1.RST
  N2: WeMos_D1_Mini1.D2, DHT22.DATA, C1.1, R4.Pin_0
  N3: WeMos_D1_Mini1.D6, U3.Trig
  N4: WeMos_D1_Mini1.D7, R2.Pin_1
  GND: WeMos_D1_Mini1.G, DHT22.GND, U3.GND, C1.0, TP4056.pin6
  N5: U3.Echo, R2.Pin_0
  N6: TP4056.pin1, D1.C
  N7: TP4056.pin2, D1.A
  N8: TP4056.pin4, U4.+
  N9: TP4056.pin5, U4.-

notes:
  JSN-SR04T

custom parts:
  HC-SR04: HC-SR04 ultrasound distance sensor
  TP4056: A DIP stand-in part for whatever IC you want. With 6 pins on a 300mil dual inline package (DIP) footprint.

// code stored in the sketch: MQTT_WeMos_Deep_Sleep_Climasensor_Ultrasonic.ino.ino
#include <ESP8266WiFi.h>
#include <WiFiClient.h>
#include <PubSubClient.h>
#include "DHT.h"
#include <NewPingESP8266.h>

#define FORCE_DEEPSLEEP
#define TIME_TO_SLEEP  1        //Time ESP32 will go to sleep (in Minutes), max 70
#define TRIGGER_PIN  D6         // Arduino pin tied to trigger pin on the ultrasonic sensor.
#define ECHO_PIN     D7         // Arduino pin tied to echo pin on the ultrasonic sensor.
#define MAX_DISTANCE 200        // Maximum distance we want to ping for (in centimeters). Maximum sensor distance is rated at 400-500cm.

#define DHTTYPE DHT22
#define DHTPIN 4

//Pin Declarations
const int gasPin = A0;                    // Luftqualitäts-Pin = A0

const char* host = "192.168.1.1";   //MQTT-Host IP
const char* ssid = "Ssid";
const char* password = "WLAN-Password";

//Variables
float t = 0.0;
float h = 0.0;
float hic = 0.0;
float dwp = 0.0;
float diff = 1.0;
float gas = 0.0;
float gasdiff = 10.0;
unsigned int batt;
double battV;
bool dhtValue = false;

DHT dht(DHTPIN, DHTTYPE);
NewPingESP8266 sonar(TRIGGER_PIN, ECHO_PIN, MAX_DISTANCE); // NewPingESP8266 setup of pins and maximum distance.

WiFiClient net;
PubSubClient mqtt(net);

void connect();


bool checkBound(float newValue, float prevValue, float maxDiff) {
  return !isnan(newValue) &&
         (newValue < prevValue - maxDiff || newValue > prevValue + maxDiff);
}

float calcDewpoint(float humi, float temp) {
  float k;
  k = log(humi / 100) + (17.62 * temp) / (243.12 + temp);
  return 243.12 * k / (17.62 - k);
}


void setup() {
  Serial.begin(115200);
  Serial.println();
  Serial.println("Booting...");

  WiFi.mode(WIFI_AP_STA);
  WiFi.begin(ssid, password);

  mqtt.setServer(host, 1883);

  dht.begin();
  delay(2000);
  connect();

  Serial.println("Setup completed...");
}

void connect() {
  // Loop until we're reconnected
  while (!mqtt.connected()) {
    Serial.print("Attempting MQTT connection...");
    // Create a random client ID
    String clientId = "ESP8266Client-";
    clientId += String(random(0xffff), HEX);
    // Attempt to connect
    if (mqtt.connect(clientId.c_str())) {
      Serial.println("connected");
      // Once connected, publish an announcement...
      mqtt.publish("Tank/state", "ready");
      // ... and resubscribe
      mqtt.subscribe("Tank/back");
    } else {
      Serial.print("failed, rc=");
      Serial.print(mqtt.state());
      Serial.println(" try again in 5 seconds");
      // Wait 5 seconds before retrying
      delay(5000);
    }
  }
}

void messageReceived(String topic, String payload, char * bytes, unsigned int length) {
  Serial.print("incoming: ");
  Serial.print(topic);
  Serial.print(" - ");
  Serial.print(payload);
  Serial.println();
}

double mapDouble(double x, double in_min, double in_max, double out_min, double out_max)
{
  double temp = (x - in_min) * (out_max - out_min) / (in_max - in_min) + out_min;
  temp = (int) (4 * temp + .5);
  return (double) temp / 4;
}

void climate() {
  float nh = dht.readHumidity();
  float nt = dht.readTemperature();
  float nhic = dht.computeHeatIndex(nt, nh, false);
  float ndwp = calcDewpoint(nh, nt);
  float ngas = analogRead(gasPin);
  int dhtValue1 = 0;
  if (isnan(nh) || isnan(nt)) {
    Serial.println("Failed to read from DHT sensor!");
    return;
  }
  if (checkBound(nt, t, diff)) {
    t = nt;
    mqtt.publish("Tank/temp", String(t).c_str(), true);
    Serial.print("Temperature: ");
    Serial.print(t);
    Serial.print(" *C ");
    Serial.println("------------------------------------");
    if (t > 0.0) {
      dhtValue1 = dhtValue1 + 1;
    }
  }
  if (checkBound(nh, h, diff)) {
    h = nh;
    mqtt.publish("Tank/humidity", String(h).c_str(), true);
    Serial.println("Dewpoint: ");
    Serial.print(h);
    Serial.print(" % ");
    Serial.println("------------------------------------");
    if (dwp > 0.0) {
      dhtValue1 = dhtValue1 + 1;
    }
  }

  if (checkBound(nhic, hic, diff)) {
    hic = nhic;
    mqtt.publish("Tank/heatindex", String(hic).c_str(), true);
    Serial.println("Heat index: ");
    Serial.print(hic);
    Serial.print(" *C ");
    Serial.println("------------------------------------");
    if (hic > 0.0) {
      dhtValue1 = dhtValue1 + 1;
    }
  }

  if (checkBound(ndwp, dwp, diff)) {
    dwp = ndwp;
    mqtt.publish("Tank/dewpoint", String(dwp).c_str(), true);
    Serial.println("DewPoint: ");
    Serial.print(dwp);
    Serial.print(" *C ");
    Serial.println("------------------------------------");
    if (dwp > 0.0) {
      dhtValue1 = dhtValue1 + 1;
    }
  }

  if (checkBound(ngas, gas, gasdiff)) {
    gas = ngas;
    mqtt.publish("Tank/luftquali", String(gas).c_str(), true);
    Serial.println("Luftqualitaet: ");
    Serial.println(gas);
    Serial.println("pph");
    Serial.println("------------------------------------");
    if (gas = 0.0) {
      dhtValue1 = dhtValue1 + 1;
    }
    if (dhtValue1 > 4) {
      dhtValue = true;
    }
    else {
      dhtValue = false;
    }
  }
}

void levelsensor() {
  int maxlevel = 250;                 // Variable to store the maximal Distance in centimeters from the bottom of the Tank to the maximal fillment
  int maxFillment = 1500;             // Varaible to store the max. Tank fillment in liters
  int DistanceSum;
  Serial.print("Starting Fillment measuring:.");

  for (int i = 1; i <= 10; i++) {
    Serial.print(".");
    int Distance = 0;
    unsigned int uS = sonar.ping();   // Send ping, get ping time in microseconds (uS).
    Distance = sonar.convert_cm(uS);  // Convert ping time to distance and print result (0 = outside set distance range, no ping echo)
    DistanceSum = DistanceSum + Distance;
    delay(1000);
  }
  Serial.println(".");
  int DistanceAverage = DistanceSum / 10;
  int Level = maxlevel - (DistanceAverage);           // Variable to calculate the height of the Level
  int liter = maxFillment / maxlevel * Level;     // Finally Value to store the effectiv fillment in liters to post over Mqtt
  Serial.println("Distance: " + String(DistanceAverage) + " Level: " + String(Level) + " liter: " + String(liter));
  mqtt.publish("Tank/content", String(liter).c_str(), true);
  mqtt.publish("Tank/level", String(Level).c_str(), true);
}

void battState() {
  batt = analogRead(A0)/1.75;
  battV = mapDouble(batt, 0, 1023, 0.0, 6.6);
  mqtt.publish("Tank/batt", String(battV).c_str(), true);
  Serial.println("Batt Volt: " + String(battV));
}

void loop() {
  if (!mqtt.connected()) {
    connect();
  }
  mqtt.loop();
  delay(10000); // time to make reprogramming possible
  battState();
  climate();
  levelsensor();
  delay(3000); // secure that the mqtt-Messages from all Functions gets sent before going to deep sleep


#ifdef FORCE_DEEPSLEEP
  if (battV < 4.8) { // Handle longer sleep times if Battery is too low
    Serial.println("Force deepsleep for " + String 70)+ " min!");
    String tts = "Force deepsleep for " + String (70) + " min!";
    mqtt.publish("Tank/state", String(tts).c_str(), true);
    delay(2000);
    ESP.deepSleep(70 * 1000000); //send IFTTT low_bat warning
  } 
  else if (battV < 4.0){
    Serial.println("Force deepsleep for " + String (TIME_TO_SLEEP) + " min!");
    String tts = "Force deepsleep for " + String (TIME_TO_SLEEP) + " min!";
    mqtt.publish("Tank/state", String(tts).c_str(), true);
    delay(2000);
    ESP.deepSleep(TIME_TO_SLEEP * 1000000);
  }
#endif
}

// code stored in the sketch: MQTT_WeMos_Deep_Sleep_Climasensor_Ultrasonic_pubSub.ino.ino
#include <ESP8266WiFi.h>
#include <WiFiClient.h>
#include <PubSubClient.h>
#include "DHT.h"
#include <NewPingESP8266.h>

#define FORCE_DEEPSLEEP
#define TIME_TO_SLEEP  1        //Time ESP32 will go to sleep (in Minutes), max 70
#define TRIGGER_PIN  D6         // Arduino pin tied to trigger pin on the ultrasonic sensor.
#define ECHO_PIN     D7         // Arduino pin tied to echo pin on the ultrasonic sensor.
#define MAX_DISTANCE 200        // Maximum distance we want to ping for (in centimeters). Maximum sensor distance is rated at 400-500cm.

#define DHTTYPE DHT22
#define DHTPIN 4

//Pin Declarations
const int gasPin = A0;                    // Luftqualitäts-Pin = A0

const char* host = "192.168.178.4";
const char* ssid = "Chickenpocks";
const char* password = "0s7v1e4n2g2a6";

//Variables
float t = 0.0;
float h = 0.0;
float hic = 0.0;
float dwp = 0.0;
float diff = 1.0;
float gas = 0.0;
float gasdiff = 10.0;
unsigned int batt;
double battV;
bool dhtValue = false;

DHT dht(DHTPIN, DHTTYPE);
NewPingESP8266 sonar(TRIGGER_PIN, ECHO_PIN, MAX_DISTANCE); // NewPingESP8266 setup of pins and maximum distance.

WiFiClient net;
PubSubClient mqtt(net);

void connect();


bool checkBound(float newValue, float prevValue, float maxDiff) {
  return !isnan(newValue) &&
         (newValue < prevValue - maxDiff || newValue > prevValue + maxDiff);
}

float calcDewpoint(float humi, float temp) {
  float k;
  k = log(humi / 100) + (17.62 * temp) / (243.12 + temp);
  return 243.12 * k / (17.62 - k);
}


void setup() {
  Serial.begin(115200);
  Serial.println();
  Serial.println("Booting...");

  WiFi.mode(WIFI_AP_STA);
  WiFi.begin(ssid, password);

  mqtt.setServer(host, 1883);

  dht.begin();
  delay(2000);
  connect();

  Serial.println("Setup completed...");
}

void connect() {
  // Loop until we're reconnected
  while (!mqtt.connected()) {
    Serial.print("Attempting MQTT connection...");
    // Create a random client ID
    String clientId = "ESP8266Client-";
    clientId += String(random(0xffff), HEX);
    // Attempt to connect
    if (mqtt.connect(clientId.c_str())) {
      Serial.println("connected");
      // Once connected, publish an announcement...
      mqtt.publish("Tank/state", "ready");
      // ... and resubscribe
      mqtt.subscribe("Tank/back");
    } else {
      Serial.print("failed, rc=");
      Serial.print(mqtt.state());
      Serial.println(" try again in 5 seconds");
      // Wait 5 seconds before retrying
      delay(5000);
    }
  }
}

void messageReceived(String topic, String payload, char * bytes, unsigned int length) {
  Serial.print("incoming: ");
  Serial.print(topic);
  Serial.print(" - ");
  Serial.print(payload);
  Serial.println();
}

double mapDouble(double x, double in_min, double in_max, double out_min, double out_max)
{
  double temp = (x - in_min) * (out_max - out_min) / (in_max - in_min) + out_min;
  temp = (int) (4 * temp + .5);
  return (double) temp / 4;
}

void climate() {
  float nh = dht.readHumidity();
  float nt = dht.readTemperature();
  float nhic = dht.computeHeatIndex(nt, nh, false);
  float ndwp = calcDewpoint(nh, nt);
  float ngas = analogRead(gasPin);
  int dhtValue1 = 0;
  if (isnan(nh) || isnan(nt)) {
    Serial.println("Failed to read from DHT sensor!");
    return;
  }
  if (checkBound(nt, t, diff)) {
    t = nt;
    mqtt.publish("Tank/temp", String(t).c_str(), true);
    Serial.print("Temperature: ");
    Serial.print(t);
    Serial.print(" *C ");
    Serial.println("------------------------------------");
    if (t > 0.0) {
      dhtValue1 = dhtValue1 + 1;
    }
  }
  if (checkBound(nh, h, diff)) {
    h = nh;
    mqtt.publish("Tank/humidity", String(h).c_str(), true);
    Serial.println("Dewpoint: ");
    Serial.print(h);
    Serial.print(" % ");
    Serial.println("------------------------------------");
    if (dwp > 0.0) {
      dhtValue1 = dhtValue1 + 1;
    }
  }

  if (checkBound(nhic, hic, diff)) {
    hic = nhic;
    mqtt.publish("Tank/heatindex", String(hic).c_str(), true);
    Serial.println("Heat index: ");
    Serial.print(hic);
    Serial.print(" *C ");
    Serial.println("------------------------------------");
    if (hic > 0.0) {
      dhtValue1 = dhtValue1 + 1;
    }
  }

  if (checkBound(ndwp, dwp, diff)) {
    dwp = ndwp;
    mqtt.publish("Tank/dewpoint", String(dwp).c_str(), true);
    Serial.println("DewPoint: ");
    Serial.print(dwp);
    Serial.print(" *C ");
    Serial.println("------------------------------------");
    if (dwp > 0.0) {
      dhtValue1 = dhtValue1 + 1;
    }
  }

  if (checkBound(ngas, gas, gasdiff)) {
    gas = ngas;
    mqtt.publish("Tank/luftquali", String(gas).c_str(), true);
    Serial.println("Luftqualitaet: ");
    Serial.println(gas);
    Serial.println("pph");
    Serial.println("------------------------------------");
    if (gas = 0.0) {
      dhtValue1 = dhtValue1 + 1;
    }
    if (dhtValue1 > 4) {
      dhtValue = true;
    }
    else {
      dhtValue = false;
    }
  }
}

void levelsensor() {
  int maxlevel = 250;                 // Variable to store the maximal Distance in centimeters from the bottom of the Tank to the maximal fillment
  int maxFillment = 1500;             // Varaible to store the max. Tank fillment in liters
  int DistanceSum;
  Serial.print("Starting Fillment measuring:.");

  for (int i = 1; i <= 10; i++) {
    Serial.print(".");
    int Distance = 0;
    unsigned int uS = sonar.ping();   // Send ping, get ping time in microseconds (uS).
    Distance = sonar.convert_cm(uS);  // Convert ping time to distance and print result (0 = outside set distance range, no ping echo)
    DistanceSum = DistanceSum + Distance;
    delay(1000);
  }
  Serial.println(".");
  int DistanceAverage = DistanceSum / 10;
  int Level = maxlevel - (DistanceAverage);           // Variable to calculate the height of the Level
  int liter = maxFillment / maxlevel * Level;     // Finally Value to store the effectiv fillment in liters to post over Mqtt
  Serial.println("Distance: " + String(DistanceAverage) + " Level: " + String(Level) + " liter: " + String(liter));
  mqtt.publish("Tank/content", String(liter).c_str(), true);
  mqtt.publish("Tank/level", String(Level).c_str(), true);
}

void battState() {
  batt = analogRead(A0)/1.75;
  battV = mapDouble(batt, 0, 1023, 0.0, 6.6);
  mqtt.publish("Tank/batt", String(battV).c_str(), true);
  Serial.println("Batt Volt: " + String(battV));
}

void loop() {
  if (!mqtt.connected()) {
    connect();
  }
  mqtt.loop();
  delay(10000); // time to make reprogramming possible
  battState();
  climate();
  levelsensor();
  delay(3000); // secure that the mqtt-Messages from all Functions gets sent before going to deep sleep


#ifdef FORCE_DEEPSLEEP
  if (battV < 3.2) { // Handle longer sleep times if Battery is too low
    Serial.println("Force deepsleep for " + String (TIME_TO_SLEEP*2)+ " min!");
    String tts = "Force deepsleep for " + String (TIME_TO_SLEEP*2) + " min!";
    mqtt.publish("Tank/state", String(tts).c_str(), true);
    delay(2000);
    ESP.deepSleep((TIME_TO_SLEEP/2) * 1000000); //send IFTTT low_bat warning
  } 
  else if (battV < 4.0){
    Serial.println("Force deepsleep for " + String (TIME_TO_SLEEP) + " min!");
    String tts = "Force deepsleep for " + String (TIME_TO_SLEEP) + " min!";
    mqtt.publish("Tank/state", String(tts).c_str(), true);
    delay(2000);
    ESP.deepSleep(TIME_TO_SLEEP * 1000000);
  }
#endif
}
